// Digital circuit mcpu16_term.dig as structural Verilog
module mcpu16_term (
  input  relogio,
  output [31:0] cnt
);

  wire add_2_c_o, and_1_out, C, d14, d15, d_ff_1_q, grava, hA, hC, hCI, hE, limpC, not_3_out, not_4_out,
       register_1_q, register_2_q, sULA;
  wire [13:0] add_1_s, CI_q, E_q, multiplexer_1_out, termcnt_1_dout;
  wire [15:0] A_q, add_2_s, multiplexer_2_out, nor_1_out, ramdualport_1_d;

  Add #(.Bits(14)) add_1 (.a(E_q), .b({14{1'b0}}), .c_i(1'b1), .s(add_1_s));  // open: c_o
  Register #(.Bits(14)) CI (.D(add_1_s), .C(relogio), .en(hCI), .Q(CI_q));
  assign nor_1_out = ~({d15, d14, termcnt_1_dout} | A_q);  // NOr nor_1, 16 bits wide
  Register register_1 (.D(d14), .C(relogio), .en(hCI), .Q(register_1_q));
  Register register_2 (.D(d15), .C(relogio), .en(hCI), .Q(register_2_q));
  D_FF d_ff_1 (.D(hCI), .C(relogio), .Q(d_ff_1_q), .nQ(hCI));
  Add #(.Bits(16)) add_2 (.a({d15, d14, termcnt_1_dout}), .b(A_q), .c_i(1'b0), .s(add_2_s), .c_o(add_2_c_o));
  Multiplexer #(.Bits(14)) multiplexer_1 (.sel(hCI), .in_0(CI_q), .in_1(termcnt_1_dout), .out(multiplexer_1_out));
  and and_1 (and_1_out, limpC, add_2_c_o);
  not not_1 (sULA, register_1_q);
  not not_2 (limpC, register_2_q);
  Multiplexer #(.Bits(16)) multiplexer_2 (.sel(sULA), .in_0(add_2_s), .in_1(nor_1_out), .out(multiplexer_2_out));
  Register #(.Bits(14)) E (.D(multiplexer_1_out), .C(relogio), .en(hE), .Q(E_q));
  Register u_C (.D(and_1_out), .C(relogio), .en(hC), .Q(C));
  Register #(.Bits(16)) A (.D(multiplexer_2_out), .C(relogio), .en(hA), .Q(A_q));
  not not_3 (not_3_out, C);
  and and_2 (hC, register_1_q, d_ff_1_q);
  and and_3 (hA, d_ff_1_q, limpC);
  and and_4 (grava, d_ff_1_q, register_2_q, sULA);
  nand nand_1 (hE, d_ff_1_q, register_1_q, register_2_q, not_3_out);
  RAMDualPort #(.AddrBits(14), .isProgramMemory("true"), .Bits(16)) ramdualport_1 (
    .A(E_q), .Din(A_q), .str(grava), .C(relogio), .ld(1'b1), .D(ramdualport_1_d));
  not not_4 (not_4_out, grava);
  termcnt termcnt_1 (
    .relogio(relogio), .write(grava), .read(not_4_out), .Addr({{18{1'b1}}, E_q}), .dMemOut(ramdualport_1_d),
    .dIn(A_q), .dOut({d15, d14, termcnt_1_dout}), .cnt(cnt));

  // Other names for the same wires on the sheet: sE = hCI

  // Notes on the sheet:
  //   relogio: Hz: 2147483647
  //   cnt: clock cycles for benchmark
endmodule
