// Digital circuit mcpu_bram.dig as structural Verilog
module mcpu_bram (
  input  clk
);

  wire add_2_c_o, and_1_out, and_2_out, and_3_out, and_4_out, C_q, d_ff_1_nq, d_ff_1_q, d_ff_2_nq, eAk, eC,
       ePC, i6, i7, sA, wr;
  wire [5:0] add_1_s, IR_q, multiplexer_1_out, multiplexer_3_out, PC_q;
  wire [7:0] add_2_s, Akku_q, blockramdualport_1_d, multiplexer_2_out, nor_1_out;

  and and_1 (and_1_out, d_ff_1_q, d_ff_2_nq);
  Register #(.Bits(8)) IR (.D(blockramdualport_1_d), .C(clk), .en(d_ff_1_q), .Q({i7, i6, IR_q}));
  D_FF d_ff_1 (.D(and_3_out), .C(clk), .Q(d_ff_1_q), .nQ(d_ff_1_nq));
  D_FF d_ff_2 (.D(and_1_out), .C(clk), .Q(sA), .nQ(d_ff_2_nq));
  // Probe instr on {i7, i6, IR_q}
  // Probe fetch on d_ff_1_q
  // Probe mem on sA
  Add #(.Bits(6)) add_1 (.a(multiplexer_3_out), .b({6{1'b0}}), .c_i(1'b1), .s(add_1_s));  // open: c_o
  assign nor_1_out = ~(Akku_q | blockramdualport_1_d);  // NOr nor_1, 8 bits wide
  Add #(.Bits(8)) add_2 (.a(Akku_q), .b(blockramdualport_1_d), .c_i(1'b0), .s(add_2_s), .c_o(add_2_c_o));
  and and_2 (and_2_out, add_2_c_o, ~i7);  // And
  and and_3 (and_3_out, d_ff_1_nq, d_ff_2_nq);
  Multiplexer #(.Bits(6)) multiplexer_1 (.sel(sA), .in_0(add_1_s), .in_1(IR_q), .out(multiplexer_1_out));
  Multiplexer #(.Bits(8)) multiplexer_2 (.sel(i6), .in_0(nor_1_out), .in_1(add_2_s), .out(multiplexer_2_out));
  Register #(.Bits(6)) PC (.D(multiplexer_1_out), .C(clk), .en(ePC), .Q(PC_q));
  Register #(.Bits(8)) Akku (.D(multiplexer_2_out), .C(clk), .en(eAk), .Q(Akku_q));
  Register C (.D(and_2_out), .C(clk), .en(eC), .Q(C_q));
  // Probe exec on and_3_out
  Multiplexer #(.Bits(6)) multiplexer_3 (.sel(sA), .in_0(PC_q), .in_1(IR_q), .out(multiplexer_3_out));
  and and_4 (and_4_out, sA, i6, i7, ~C_q);  // And
  // Probe A on multiplexer_3_out
  // Probe Din on Akku_q
  and and_5 (wr, sA, ~i6, i7);  // And
  and and_6 (eAk, and_3_out, ~i7);  // And
  and and_7 (eC, i6, and_3_out);
  or or_1 (ePC, d_ff_1_q, and_4_out);
  BlockRAMDualPort #(.AddrBits(6), .isProgramMemory("true"), .Bits(8)) blockramdualport_1 (
    .A(multiplexer_3_out), .Din(Akku_q), .str(wr), .C(clk), .D(blockramdualport_1_d));
  // Probe wr on wr
  // Probe Dout on blockramdualport_1_d

  // Other names for the same wires on the sheet: sAk = i6

  // Notes on the sheet:
  //   Control Unit
  //   Data Path
endmodule
