// Digital circuit ncpu_terminal.dig as structural Verilog
module ncpu_terminal (
  input  clock
);

  wire and_1_out, and_2_out, C, eF, eI, eP, eR0, eR1, eR2, wr, Z;
  wire [1:0] sA, sB;
  wire [3:0] offset, op;
  wire [7:0] alu_1_r, instr, multiplexer_1_out, multiplexer_2_out, p_q, r0_q, r1_q, r2_q, ramdualport_1_d;

  Register #(.Bits(8)) IR (.D(ramdualport_1_d), .C(clock), .en(eI), .Q(instr));
  Register #(.Bits(8)) r0 (.D(alu_1_r), .C(clock), .en(eR0), .Q(r0_q));
  Register #(.Bits(8)) r1 (.D(alu_1_r), .C(clock), .en(eR1), .Q(r1_q));
  Register #(.Bits(8)) r2 (.D(alu_1_r), .C(clock), .en(eR2), .Q(r2_q));
  Register #(.Bits(8)) p (.D(alu_1_r), .C(clock), .en(eP), .Q(p_q));
  Multiplexer #(.Bits(8), .Selector_Bits(2)) multiplexer_1 (
    .sel(sA), .in_0(r0_q), .in_1(r1_q), .in_2(r2_q), .in_3({4'b0000, offset}), .out(multiplexer_1_out));
  Multiplexer #(.Selector_Bits(2), .Bits(8)) multiplexer_2 (
    .sel(sB), .in_0(r0_q), .in_1(r1_q), .in_2(r2_q), .in_3(p_q), .out(multiplexer_2_out));
  and and_1 (and_1_out, multiplexer_2_out[0], multiplexer_2_out[1], multiplexer_2_out[2], multiplexer_2_out[3], multiplexer_2_out[4], multiplexer_2_out[5], multiplexer_2_out[6], multiplexer_2_out[7]);
  RAMDualPort #(.AddrBits(8), .Bits(8), .isProgramMemory("true")) ramdualport_1 (
    .A(multiplexer_2_out), .Din(multiplexer_1_out), .str(wr), .C(clock), .ld(1'b1), .D(ramdualport_1_d));
  alu alu_1 (
    .op(op), .A(multiplexer_1_out), .B(multiplexer_2_out), .R(alu_1_r), .clk(clock), .Z(Z), .C(C),
    .eFlags(eF), .M(ramdualport_1_d));
  and and_2 (and_2_out, and_1_out, wr);
  Terminal terminal_1 (.D(multiplexer_1_out), .C(clock), .en(and_2_out));
  // Probe on instr
  // Probe on Z
  // Probe on C
  DipSwitch dipswitch_1 (.out(op[0]));
  DipSwitch dipswitch_2 (.out(op[1]));
  DipSwitch dipswitch_3 (.out(op[2]));
  DipSwitch dipswitch_4 (.out(op[3]));
  DipSwitch dipswitch_5 (.out(offset[0]));
  DipSwitch dipswitch_6 (.out(offset[1]));
  DipSwitch dipswitch_7 (.out(offset[2]));
  DipSwitch dipswitch_8 (.out(offset[3]));
  DipSwitch dipswitch_9 (.out(wr));
  DipSwitch dipswitch_10 (.out(eF));
  DipSwitch dipswitch_11 (.out(eI));
  DipSwitch dipswitch_12 (.out(eR0));
  DipSwitch dipswitch_13 (.out(eR1));
  DipSwitch dipswitch_14 (.out(eR2));
  DipSwitch dipswitch_15 (.out(eP));
  DipSwitch dipswitch_16 (.out(sA[0]));
  DipSwitch dipswitch_17 (.out(sA[1]));
  DipSwitch dipswitch_18 (.out(sB[0]));
  DipSwitch dipswitch_19 (.out(sB[1]));
endmodule
