// Digital circuit ncpu16.dig as structural Verilog
// A very simple 16 bit processor
module ncpu16 (
  input  reset,
  input  clock,
  input  [15:0] dIn,
  output [15:0] address,
  output wr,
  output rd,
  output [15:0] dOut
);

  wire IR4, IR5, IR6, mem, w0, w1, w2, w3, w4, w5, w6, wPC;
  wire [1:0] shft;
  wire [2:0] rA, rB;
  wire [3:0] undriven_2;
  wire [11:0] undriven_4;
  wire [14:0] undriven_3;
  wire [15:0] add_1_s, and_1_out, multiplexer_1_out, multiplexer_3_out, multiplexer_4_out, multiplexer_5_out,
       multiplexer_6_out, multiplexer_7_out, not_1_out, offset, or_1_out, PC_q, r0_q, r1_q, r2_q, r3_q, r4_q,
       r5_q, r6_q, xor_1_out;
  wire [15:15] undriven;

  Multiplexer #(.Bits(16)) multiplexer_1 (.sel(mem), .in_0(address), .in_1(dIn), .out(multiplexer_1_out));
  Register #(.Bits(16)) r0 (.D(multiplexer_1_out), .C(clock), .en(w0), .Q(r0_q));
  Register #(.Bits(16)) r1 (.D(multiplexer_1_out), .C(clock), .en(w1), .Q(r1_q));
  Register #(.Bits(16)) r2 (.D(multiplexer_1_out), .C(clock), .en(w2), .Q(r2_q));
  Register #(.Bits(16)) r3 (.D(multiplexer_1_out), .C(clock), .en(w3), .Q(r3_q));
  Register #(.Bits(16)) r4 (.D(multiplexer_1_out), .C(clock), .en(w4), .Q(r4_q));
  Register #(.Bits(16)) r5 (.D(multiplexer_1_out), .C(clock), .en(w5), .Q(r5_q));
  Register #(.Bits(16)) r6 (.D(multiplexer_1_out), .C(clock), .en(w6), .Q(r6_q));
  Register #(.Bits(16)) PC (.D(multiplexer_1_out), .C(clock), .en(wPC), .Q(PC_q));
  Multiplexer #(.Bits(16), .Selector_Bits(3)) multiplexer_2 (
    .sel(rA), .in_0(r0_q), .in_1(r1_q), .in_2(r2_q), .in_3(r3_q), .in_4(r4_q), .in_5(r5_q), .in_6(r6_q),
    .in_7(PC_q), .out(dOut));
  Multiplexer #(.Selector_Bits(3), .Bits(16)) multiplexer_3 (
    .sel(rB), .in_0(r0_q), .in_1(r1_q), .in_2(r2_q), .in_3(r3_q), .in_4(r4_q), .in_5(r5_q), .in_6(r6_q),
    .in_7(PC_q), .out(multiplexer_3_out));
  assign and_1_out = dOut & multiplexer_3_out;  // And and_1, 16 bits wide
  assign or_1_out = dOut | multiplexer_3_out;  // Or or_1, 16 bits wide
  assign xor_1_out = dOut ^ multiplexer_3_out;  // XOr xor_1, 16 bits wide
  assign not_1_out = ~multiplexer_3_out;  // Not not_1, 16 bits wide
  Multiplexer #(.Bits(16)) multiplexer_4 (.sel(mem), .in_0(dOut), .in_1(offset), .out(multiplexer_4_out));
  Multiplexer #(.Bits(16), .Selector_Bits(2)) multiplexer_5 (
    .sel({IR4, IR5}), .in_0(multiplexer_3_out), .in_1(not_1_out), .in_2(16'h1), .in_3(16'hfffe),
    .out(multiplexer_5_out));
  Multiplexer #(.Selector_Bits(2), .Bits(16)) multiplexer_6 (
    .sel({IR4, IR5}), .in_0(multiplexer_3_out), .in_1(and_1_out), .in_2(or_1_out), .in_3(xor_1_out),
    .out(multiplexer_6_out));
  Add #(.Bits(16)) add_1 (.a(multiplexer_4_out), .b(multiplexer_5_out), .c_i(IR4), .s(add_1_s));  // open: c_o
  Multiplexer #(.Bits(16)) multiplexer_7 (.sel(IR6), .in_0(add_1_s), .in_1(multiplexer_6_out), .out(multiplexer_7_out));
  Multiplexer #(.Bits(16), .Selector_Bits(2)) multiplexer_8 (
    .sel(shft), .in_0(multiplexer_7_out), .in_1({undriven[15], undriven_3}), .in_2({undriven_2, undriven_4}),
    .in_3({multiplexer_7_out[7:0], multiplexer_7_out[15:8]}), .out(address));

  // Notes on the sheet:
  //   address: selects memory word to read or write
  //   wr: this cycle will write a word to memory
  //   rd: this cycle will read a word from memory
  //   dOut: data to memory
  //   dIn: data from memory
endmodule
