// Digital circuit system.dig as structural Verilog
module system (
  input  clock
);

  wire ncpu16_1_wr, reset_out;
  wire [15:0] blockramdualport_1_d, ncpu16_1_address, ncpu16_1_dout;

  ncpu16 ncpu16_1 (
    .reset(reset_out), .clock(clock), .dIn(blockramdualport_1_d), .address(ncpu16_1_address),
    .wr(ncpu16_1_wr), .dOut(ncpu16_1_dout));  // open: rd
  DipSwitch reset (.out(reset_out));
  BlockRAMDualPort #(.AddrBits(16), .isProgramMemory("true"), .Bits(16)) blockramdualport_1 (
    .A(ncpu16_1_address), .Din(ncpu16_1_dout), .str(ncpu16_1_wr), .C(clock), .D(blockramdualport_1_d));
endmodule
