// Digital circuit darkriscvTerm.dig as structural Verilog
module darkriscvTerm (
);

  darkriscv #(.applicationType("IVERILOG"), .CodeFile("/home/jecel/mygit/digitalCPUzoo/RV-Wrappers/src/darkriscv/darkriscv.v")) u_darkriscv ();  // open: RES, CLK, HLT, IDATA, DATAI, IADDR, DATAO, BE, WR, RD, IDLE, DEBUG
  termcnt termcnt_1 ();  // open: relogio, write, read, Addr, dMemOut, dIn, dOut, cnt
endmodule
