// Digital circuit av.dig as structural Verilog
// This uses a 4K x 16 bit external memory to generate the timing for a 1280x720 image with
// 80x30 characters, each 16x26 pixels in size. It also generates a new 16 bit audio sample
// on each horizontal line (45 KHz)
module av (
  input  [15:0] dIn,
  input  pclk,
  output [7:0] R,
  output [7:0] G,
  output [7:0] B,
  output H,
  output V,
  output [11:0] X,
  output [11:0] Y,
  output sclk,
  output [15:0] left,
  output [15:0] right,
  output read,
  output [11:0] Addr
);

  wire and_1_out, and_2_out, and_3_out, and_4_out, and_5_out, and_6_out, nor_1_out, not_1_out, sub_1_c_o,
       sub_2_c_o, sub_3_c_o, sub_4_c_o, sub_5_c_o, sub_6_c_o, sub_7_c_o, sub_8_c_o;
  wire [4:0] add_3_s, add_4_s, cRow, cY, multiplexer_5_out, multiplexer_6_out;
  wire [7:0] multiplexer_1_out, multiplexer_8_out, multiplexer_9_out, multiplexer_10_out, register_1_q;
  wire [9:8] not_3_out;
  wire [11:0] add_1_s, add_2_s, multiplexer_3_out, multiplexer_4_out;
  wire [15:0] multiplexer_2_out, register_2_q;

  Multiplexer #(.Bits(8)) multiplexer_1 (.sel(X[4]), .in_0(dIn[7:0]), .in_1(dIn[15:8]), .out(multiplexer_1_out));
  and and_1 (and_1_out, ~X[0], and_2_out);  // And
  and and_2 (and_2_out, ~X[1], ~X[2], ~X[3]);  // And
  and and_3 (and_3_out, X[0], and_2_out);
  Add #(.Bits(12)) add_1 (.a(X), .b({12{1'b0}}), .c_i(1'b1), .s(add_1_s));  // open: c_o
  Add #(.Bits(12)) add_2 (.a(Y), .b({12{1'b0}}), .c_i(1'b1), .s(add_2_s));  // open: c_o
  Add #(.Bits(5)) add_3 (.a(cRow), .b({5{1'b0}}), .c_i(1'b1), .s(add_3_s));  // open: c_o
  Add #(.Bits(5)) add_4 (.a(cY), .b({5{1'b0}}), .c_i(1'b1), .s(add_4_s));  // open: c_o
  Register #(.Bits(8)) register_1 (.D(multiplexer_1_out), .C(pclk), .en(and_1_out), .Q(register_1_q));
  Multiplexer #(.Bits(16)) multiplexer_2 (
    .sel(and_3_out), .in_0({register_2_q[14:0], 1'b0}), .in_1(dIn), .out(multiplexer_2_out));
  Multiplexer #(.Bits(12)) multiplexer_3 (.sel(sub_4_c_o), .in_0({12{1'b0}}), .in_1(add_1_s), .out(multiplexer_3_out));
  not not_1 (not_1_out, sub_4_c_o);
  Multiplexer #(.Bits(12)) multiplexer_4 (.sel(sub_8_c_o), .in_0({12{1'b0}}), .in_1(add_2_s), .out(multiplexer_4_out));
  Multiplexer #(.Bits(5)) multiplexer_5 (.sel(nor_1_out), .in_0({5{1'b0}}), .in_1(add_3_s), .out(multiplexer_5_out));
  Multiplexer #(.Bits(5)) multiplexer_6 (.sel(sub_8_c_o), .in_0({5{1'b0}}), .in_1(add_4_s), .out(multiplexer_6_out));
  Register #(.Bits(16)) register_2 (.D(multiplexer_2_out), .C(pclk), .en(1'b1), .Q(register_2_q));
  Register #(.Bits(12)) u_x (.D(multiplexer_3_out), .C(pclk), .en(1'b1), .Q(X));
  Register #(.Bits(12)) u_y (.D(multiplexer_4_out), .C(pclk), .en(not_1_out), .Q(Y));
  Register #(.Bits(5)) u_cRow (.D(multiplexer_5_out), .C(pclk), .en(not_1_out), .Q(cRow));
  Register #(.Bits(5)) u_cY (.D(multiplexer_6_out), .C(pclk), .en(and_5_out), .Q(cY));
  not not_2 (not_3_out[8], cRow[3]);
  not not_3 (not_3_out[9], cRow[4]);
  Sub #(.Bits(12)) sub_1 (.a(X), .b(12'h500), .c_i(1'b0), .c_o(sub_1_c_o));  // open: s
  Sub #(.Bits(12)) sub_2 (.a(X), .b(12'h56e), .c_i(1'b0), .c_o(sub_2_c_o));  // open: s
  Sub #(.Bits(12)) sub_3 (.a(X), .b(12'h596), .c_i(1'b0), .c_o(sub_3_c_o));  // open: s
  Sub #(.Bits(12)) sub_4 (.a(X), .b(12'h671), .c_i(1'b0), .c_o(sub_4_c_o));  // open: s
  Sub #(.Bits(12)) sub_5 (.a(Y), .b(12'h2d0), .c_i(1'b0), .c_o(sub_5_c_o));  // open: s
  Sub #(.Bits(12)) sub_6 (.a(Y), .b(12'h2d5), .c_i(1'b0), .c_o(sub_6_c_o));  // open: s
  Sub #(.Bits(12)) sub_7 (.a(Y), .b(12'h2da), .c_i(1'b0), .c_o(sub_7_c_o));  // open: s
  Sub #(.Bits(12)) sub_8 (.a(Y), .b(12'h2ed), .c_i(1'b0), .c_o(sub_8_c_o));  // open: s
  and and_4 (and_4_out, cRow[0], cRow[1], cRow[2], ~cRow[3], cRow[4]);  // And
  and and_5 (and_5_out, ~nor_1_out, not_1_out);  // And
  and and_6 (and_6_out, sub_1_c_o, sub_5_c_o);
  and and_7 (H, ~sub_2_c_o, sub_3_c_o);  // And
  and and_8 (V, ~sub_6_c_o, sub_7_c_o);  // And
  nor nor_1 (nor_1_out, ~sub_8_c_o, and_4_out);  // NOr
  Multiplexer #(.Bits(12)) multiplexer_7 (
    .sel(and_3_out), .in_0({X[11:5], cY}),
    .in_1({register_1_q[6:5], not_3_out, register_1_q[4:0], cRow[2:0]}), .out(Addr));
  Multiplexer #(.Bits(8)) multiplexer_8 (
    .sel(register_2_q[15]), .in_0({8{1'b0}}), .in_1({8{1'b1}}), .out(multiplexer_8_out));
  Multiplexer #(.Bits(8)) multiplexer_9 (
    .sel(register_2_q[15]), .in_0({8{1'b0}}), .in_1({8{1'b1}}), .out(multiplexer_9_out));
  Multiplexer #(.Bits(8)) multiplexer_10 (
    .sel(register_2_q[15]), .in_0({8{1'b0}}), .in_1({8{1'b1}}), .out(multiplexer_10_out));
  Multiplexer #(.Bits(8)) multiplexer_11 (.sel(and_6_out), .in_0({8{1'b0}}), .in_1(multiplexer_8_out), .out(R));
  Multiplexer #(.Bits(8)) multiplexer_12 (.sel(and_6_out), .in_0({8{1'b0}}), .in_1(multiplexer_9_out), .out(G));
  Multiplexer #(.Bits(8)) multiplexer_13 (.sel(and_6_out), .in_0({8{1'b0}}), .in_1(multiplexer_10_out), .out(B));

  assign left = {16{1'b0}};
  assign read = 1'b1;
  assign right = {16{1'b0}};
  assign sclk = 1'b0;

  // Notes on the sheet:
  //   pclk: Hz: 500
  //   60 Hz, 74.25 MHz, 45 KHz, 1280, 110, 40, 220, 720, 5, 5, 20, false, false
endmodule
