// Digital circuit t2h.dig as structural Verilog
// The T2H processor is a one clock Harvard 16 bit implementation of a small subset of the Inmos Transputer
module t2h (
  input  reset,
  input  clock,
  input  [7:0] Inst,
  input  [15:0] dIn,
  output [15:0] I,
  output [15:0] Addr,
  output wr,
  output rd,
  output [15:0] dOut
);

  wire and_4_out, clrO, eA, eB, eC, eW, negO, or_1_out, or_2_out, or_3_out, or_4_out, or_5_out, or_8_out,
       or_9_out, or_10_out, or_11_out, s_plus, sA, sAddr, sB, sW, xor_3_out;
  wire [0:0] multiplexer_5_out, nor_1_out;
  wire [1:0] sDout, sI;
  wire [3:0] or_6_out, sALU, xor_2_out, xor_2_out_2, xor_2_out_3, xor_2_out_4;
  wire [3:3] and_2_out;
  wire [4:0] op;
  wire [7:0] multiplexer_2_out, not_1_out;
  wire [11:0] multiplexer_4_out;
  wire [15:0] A, add_1_s, add_2_s, add_4_s, add_5_s, add_6_s, and_3_out, B, C, I_plus_1, multiplexer_3_out,
       multiplexer_6_out, multiplexer_7_out, multiplexer_8_out, multiplexer_9_out, multiplexer_10_out,
       multiplexer_11_out, or_7_out, sub_1_s, W_q, xor_1_out;
  wire [15:4] x;

  or or_1 (or_1_out, A[0], A[1], A[2], A[3]);
  or or_2 (or_2_out, A[4], A[5], A[6], A[7]);
  or or_3 (or_3_out, A[8], A[9], A[10], A[11]);
  or or_4 (or_4_out, A[12], A[13], A[14], A[15]);
  or or_5 (or_5_out, or_1_out, or_2_out, or_3_out, or_4_out);
  and and_1 (op[4], Inst[4], Inst[5], Inst[6], Inst[7]);
  and and_2 (and_2_out[3], ~Inst[4], Inst[5], or_5_out, ~Inst[6], Inst[7]);  // And
  assign or_6_out = Inst[7:4] | {4{and_2_out[3]}};  // Or or_6, 4 bits wide
  assign xor_1_out = A ^ B;  // XOr xor_1, 16 bits wide
  Add #(.Bits(16)) add_1 (.a(A), .b(B), .c_i(1'b0), .s(add_1_s));  // open: c_o
  assign and_3_out = A & B;  // And and_3, 16 bits wide
  Add #(.Bits(16)) add_2 (.a(A), .b({x, Inst[3:0]}), .c_i(1'b0), .s(add_2_s));  // open: c_o
  Sub #(.Bits(16)) sub_1 (.a(B), .b(A), .c_i(1'b0), .s(sub_1_s));  // open: c_o
  assign or_7_out = A | B;  // Or or_7, 16 bits wide
  assign {xor_2_out_4, xor_2_out_3, xor_2_out_2, xor_2_out} = A ^ {x, Inst[3:0]};  // XOr xor_2, 16 bits wide
  Multiplexer #(.Bits(4)) multiplexer_1 (.sel(op[4]), .in_0(or_6_out), .in_1(Inst[3:0]), .out(op[3:0]));
  xor xor_3 (xor_3_out, A[15], B[15]);
  Multiplexer #(.Bits(8)) multiplexer_2 (.sel(negO), .in_0(x[11:4]), .in_1(not_1_out), .out(multiplexer_2_out));
  assign not_1_out = ~x[11:4];  // Not not_1, 8 bits wide
  Multiplexer #(.Selector_Bits(4), .Bits(16)) multiplexer_3 (
    .sel(sALU), .in_0(B), .in_1({A[14:0], 1'b0}), .in_2({{2{A[15]}}, A[14:1]}), .in_3(xor_1_out),
    .in_4({x, Inst[3:0]}), .in_5(add_1_s), .in_6(I_plus_1), .in_7(and_3_out), .in_8(add_2_s),
    .in_9({{15{1'b0}}, multiplexer_5_out[0]}), .in_10({{15{1'b0}}, nor_1_out[0]}), .in_11(or_7_out),
    .in_12(sub_1_s), .in_13({A[7:0], A[15:8]}), .in_14(C), .in_15(Addr), .out(multiplexer_3_out));
  and and_4 (and_4_out, ~sub_1_s[15], ~nor_1_out[0]);  // And
  or or_8 (or_8_out, xor_2_out[0], xor_2_out[1], xor_2_out[2], xor_2_out[3]);
  or or_9 (or_9_out, xor_2_out_2[0], xor_2_out_2[1], xor_2_out_2[2], xor_2_out_2[3]);
  or or_10 (or_10_out, xor_2_out_3[0], xor_2_out_3[1], xor_2_out_3[2], xor_2_out_3[3]);
  or or_11 (or_11_out, xor_2_out_4[0], xor_2_out_4[1], xor_2_out_4[2], xor_2_out_4[3]);
  Multiplexer #(.Bits(12)) multiplexer_4 (
    .sel(clrO), .in_0({12{1'b0}}), .in_1({multiplexer_2_out, Inst[3:0]}), .out(multiplexer_4_out));
  Multiplexer multiplexer_5 (.sel(xor_3_out), .in_0(and_4_out), .in_1(A[15]), .out(multiplexer_5_out[0]));
  Register #(.Bits(12)) O (.D(multiplexer_4_out), .C(clock), .en(1'b1), .Q(x));
  nor nor_1 (nor_1_out[0], or_8_out, or_9_out, or_10_out, or_11_out);
  Add #(.Bits(16)) add_3 (.a(I), .b({16{1'b0}}), .c_i(1'b1), .s(I_plus_1));  // open: c_o
  Add #(.Bits(16)) add_4 (.a(I), .b({x, Inst[3:0]}), .c_i(1'b1), .s(add_4_s));  // open: c_o
  Add #(.Bits(16)) add_5 (.a({x, Inst[3:0]}), .b(W_q), .c_i(1'b0), .s(add_5_s));  // open: c_o
  // Probe x on {x, Inst[3:0]}
  Multiplexer #(.Selector_Bits(2), .Bits(16)) multiplexer_6 (
    .sel(sI), .in_0(I_plus_1), .in_1(add_4_s), .in_2(A), .in_3(dIn), .out(multiplexer_6_out));
  Multiplexer #(.Bits(16)) multiplexer_7 (.sel(sA), .in_0(dIn), .in_1(multiplexer_3_out), .out(multiplexer_7_out));
  Multiplexer #(.Bits(16)) multiplexer_8 (.sel(sB), .in_0(A), .in_1(C), .out(multiplexer_8_out));
  t2hcontrol t2hcontrol_1 (
    .op4(op[4]), .op3(op[3]), .op2(op[2]), .op1(op[1]), .op0(op[0]), .eA(eA), .eB(eB), .eC(eC), .eW(eW),
    .sA(sA), .sALU3(sALU[3]), .sALU2(sALU[2]), .sALU1(sALU[1]), .sALU0(sALU[0]), .sB(sB), .clrO(clrO),
    .negO(negO), .sW(sW), .s_plus(s_plus), .sAddr(sAddr), .rd(rd), .wr(wr), .sDout1(sDout[1]),
    .sDout0(sDout[0]), .sI1(sI[1]), .sI0(sI[0]));
  Multiplexer #(.Bits(16)) multiplexer_9 (.sel(sW), .in_0(add_5_s), .in_1(A), .out(multiplexer_9_out));
  Multiplexer #(.Bits(16)) multiplexer_10 (.sel(s_plus), .in_0(W_q), .in_1(A), .out(multiplexer_10_out));
  Multiplexer #(.Bits(16)) multiplexer_11 (
    .sel(reset), .in_0(multiplexer_6_out), .in_1({16{1'b0}}), .out(multiplexer_11_out));
  Register #(.Bits(16)) u_I (.D(multiplexer_11_out), .C(clock), .en(1'b1), .Q(I));
  Register #(.Bits(16)) W (.D(multiplexer_9_out), .C(clock), .en(eW), .Q(W_q));
  Add #(.Bits(16)) add_6 (
    .a(multiplexer_10_out), .b({x[14:4], Inst[3:0], 1'b0}), .c_i(1'b0), .s(add_6_s));  // open: c_o
  Register #(.Bits(16)) u_A (.D(multiplexer_7_out), .C(clock), .en(eA), .Q(A));
  Register #(.Bits(16)) u_B (.D(multiplexer_8_out), .C(clock), .en(eB), .Q(B));
  Register #(.Bits(16)) u_C (.D(B), .C(clock), .en(eC), .Q(C));
  // Probe W on W_q
  // Probe B on B
  // Probe C on C
  Multiplexer #(.Bits(16)) multiplexer_12 (.sel(sAddr), .in_0(W_q), .in_1(add_6_s), .out(Addr));
  Multiplexer #(.Selector_Bits(2), .Bits(16)) multiplexer_13 (
    .sel(sDout), .in_0(A), .in_1(B), .in_2(I_plus_1), .in_3(I_plus_1), .out(dOut));
  // Probe A on A

  // Other names for the same wires on the sheet: x[3:0] = Inst[3:0]

  // Notes on the sheet:
  //   I: program counter
  //   Addr: Data memory address
  //   wr: write to memory
  //   rd: indicates a read cycle from memory
  //   Inst: instruction to be executed
  //   dIn: data from memory
  //   dOut: data output to memory
endmodule
