// Digital circuit testvt.dig as structural Verilog
module testvt (
  input  pclk
);

  wire and_1_out, and_2_out, and_3_out, not_1_out, sub_1_c_o, sub_2_c_o, sub_3_c_o, sub_4_c_o, sub_5_c_o,
       sub_6_c_o, sub_7_c_o, sub_8_c_o, xor_1_out;
  wire [7:0] multiplexer_3_out, multiplexer_4_out, multiplexer_5_out, multiplexer_6_out, multiplexer_7_out,
       multiplexer_8_out;
  wire [7:6] bg, br, fb, fg, fr;
  wire [7:7] bb;
  wire [11:0] add_1_s, add_2_s, multiplexer_1_out, multiplexer_2_out, x_q, y_q;

  Add #(.Bits(12)) add_1 (
    .a({x_q[11:10], fr, fg, fb, x_q[3:0]}), .b({12{1'b0}}), .c_i(1'b1), .s(add_1_s));  // open: c_o
  Add #(.Bits(12)) add_2 (
    .a({y_q[11:9], br, bg, bb[7], y_q[3:0]}), .b({12{1'b0}}), .c_i(1'b1), .s(add_2_s));  // open: c_o
  Multiplexer #(.Bits(12)) multiplexer_1 (.sel(sub_4_c_o), .in_0({12{1'b0}}), .in_1(add_1_s), .out(multiplexer_1_out));
  not not_1 (not_1_out, sub_4_c_o);
  Multiplexer #(.Bits(12)) multiplexer_2 (.sel(sub_8_c_o), .in_0({12{1'b0}}), .in_1(add_2_s), .out(multiplexer_2_out));
  Register #(.Bits(12)) x (.D(multiplexer_1_out), .C(pclk), .en(1'b1), .Q({x_q[11:10], fr, fg, fb, x_q[3:0]}));
  Register #(.Bits(12)) y (.D(multiplexer_2_out), .C(pclk), .en(not_1_out), .Q({y_q[11:9], br, bg, bb[7], y_q[3:0]}));
  Sub #(.Bits(12)) sub_1 (.a({x_q[11:10], fr, fg, fb, x_q[3:0]}), .b(12'h500), .c_i(1'b0), .c_o(sub_1_c_o));  // open: s
  Sub #(.Bits(12)) sub_2 (.a({x_q[11:10], fr, fg, fb, x_q[3:0]}), .b(12'h56e), .c_i(1'b0), .c_o(sub_2_c_o));  // open: s
  Sub #(.Bits(12)) sub_3 (.a({x_q[11:10], fr, fg, fb, x_q[3:0]}), .b(12'h596), .c_i(1'b0), .c_o(sub_3_c_o));  // open: s
  Sub #(.Bits(12)) sub_4 (.a({x_q[11:10], fr, fg, fb, x_q[3:0]}), .b(12'h671), .c_i(1'b0), .c_o(sub_4_c_o));  // open: s
  Sub #(.Bits(12)) sub_5 (
    .a({y_q[11:9], br, bg, bb[7], y_q[3:0]}), .b(12'h2d0), .c_i(1'b0), .c_o(sub_5_c_o));  // open: s
  Sub #(.Bits(12)) sub_6 (
    .a({y_q[11:9], br, bg, bb[7], y_q[3:0]}), .b(12'h2d5), .c_i(1'b0), .c_o(sub_6_c_o));  // open: s
  Sub #(.Bits(12)) sub_7 (
    .a({y_q[11:9], br, bg, bb[7], y_q[3:0]}), .b(12'h2da), .c_i(1'b0), .c_o(sub_7_c_o));  // open: s
  Sub #(.Bits(12)) sub_8 (
    .a({y_q[11:9], br, bg, bb[7], y_q[3:0]}), .b(12'h2ed), .c_i(1'b0), .c_o(sub_8_c_o));  // open: s
  and and_1 (and_1_out, sub_1_c_o, sub_5_c_o);
  and and_2 (and_2_out, ~sub_2_c_o, sub_3_c_o);  // And
  and and_3 (and_3_out, ~sub_6_c_o, sub_7_c_o);  // And
  xor xor_1 (xor_1_out, y_q[3], x_q[3]);
  Multiplexer #(.Bits(8)) multiplexer_3 (
    .sel(xor_1_out), .in_0({br, br, br, br}), .in_1({fr, fr, fr, fr}), .out(multiplexer_3_out));
  Multiplexer #(.Bits(8)) multiplexer_4 (
    .sel(xor_1_out), .in_0({bg, bg, bg, bg}), .in_1({fg, fg, fg, fg}), .out(multiplexer_4_out));
  Multiplexer #(.Bits(8)) multiplexer_5 (
    .sel(xor_1_out), .in_0({8{bb[7]}}), .in_1({fb, fb, fb, fb}), .out(multiplexer_5_out));
  Multiplexer #(.Bits(8)) multiplexer_6 (
    .sel(and_1_out), .in_0({8{1'b0}}), .in_1(multiplexer_3_out), .out(multiplexer_6_out));
  Multiplexer #(.Bits(8)) multiplexer_7 (
    .sel(and_1_out), .in_0({8{1'b0}}), .in_1(multiplexer_4_out), .out(multiplexer_7_out));
  Multiplexer #(.Bits(8)) multiplexer_8 (
    .sel(and_1_out), .in_0({8{1'b0}}), .in_1(multiplexer_5_out), .out(multiplexer_8_out));
  VGA vga_1 (
    .R(multiplexer_6_out), .G(multiplexer_7_out), .B(multiplexer_8_out), .H(and_2_out), .V(and_3_out),
    .C(pclk));

  // Other names for the same wires on the sheet: fb[5:0] = {fb, fb, fb}; fg[5:0] = {fg, fg, fg};
  //   fr[5:0] = {fr, fr, fr}; bb[6:0] = {7{bb[7]}}; bg[5:0] = {bg, bg, bg}; br[5:0] = {br, br, br}

  // Notes on the sheet:
  //   pclk: Hz: 2147483647
  //   60, 72.25, 1280, 110, 40, 220, 720, 5, 5, 20, false, false
endmodule
