// Digital circuit bytes.dig as structural Verilog
// converts internal word data into bytes for LB, LBU and SB instructions
module bytes (
  input  [15:0] dIn,
  input  sign,
  input  word,
  input  A0,
  input  [15:0] fromRS2,
  output [15:0] dOut,
  output [15:0] toRD
);

  wire [7:0] multiplexer_4_out;
  wire [7:7] and_1_out;

  and and_1 (and_1_out[7], toRD[7], sign);
  Multiplexer #(.Bits(8)) multiplexer_1 (.sel(A0), .in_0(dIn[7:0]), .in_1(dIn[15:8]), .out(toRD[7:0]));
  Multiplexer #(.Bits(8)) multiplexer_2 (.sel(word), .in_0({8{and_1_out[7]}}), .in_1(dIn[15:8]), .out(toRD[15:8]));
  Multiplexer #(.Bits(8)) multiplexer_3 (.sel(A0), .in_0(fromRS2[7:0]), .in_1(dIn[7:0]), .out(dOut[7:0]));
  Multiplexer #(.Bits(8)) multiplexer_4 (.sel(A0), .in_0(dIn[15:8]), .in_1(fromRS2[7:0]), .out(multiplexer_4_out));
  Multiplexer #(.Bits(8)) multiplexer_5 (.sel(word), .in_0(multiplexer_4_out), .in_1(fromRS2[15:8]), .out(dOut[15:8]));

  // Notes on the sheet:
  //   dOut: word to be sent to memory
  //   dIn: word coming from memory
  //   toRD: bytes to word
  //   sign: indicates that the byte extension should be signed
  //   word: word memory access (not byte)
  //   A0: selects between even and odd bytes
  //   fromRS2: word data from register (top 8 bits will be ignored on byte access)
endmodule
