// Digital circuit controlUnit.dig as structural Verilog
// generates control signals for datapath
module controlUnit (
  input  clock,
  input  reset,
  input  [15:0] dIn,
  input  NE,
  input  GE,
  output wr,
  output rd,
  output sign,
  output word,
  output sub,
  output \logic ,
  output [1:0] logSelect,
  output [15:0] Imm,
  output selImm,
  output Azero,
  output we,
  output [3:0] Rw,
  output [3:0] Ra,
  output [3:0] Rb,
  output selRd,
  output slt
);

  wire alt, and_1_out, and_2_out, and_4_out, and_5_out, and_6_out, and_10_out, cond, d_ff_2_q, E,
       execpla_1_we, F, imm_t, IR2, IR3, JorB, multiplexer_2_out, or_1_out, or_3_out, or_7_out, or_9_out,
       prefix_q, rst, xor_1_out, zD, zS1, zS2;
  wire [1:1] nor_1_out;
  wire [3:1] multiplexer_3_out;
  wire [5:0] multiplexer_4_out;
  wire [5:1] or_4_out;
  wire [11:0] multiplexer_1_out;
  wire [12:0] execpla_1_selimm;
  wire [15:0] IM_q;
  wire [15:8] IR_q;

  Multiplexer #(.Bits(12)) multiplexer_1 (
    .sel(d_ff_2_q), .in_0({IR_q, Rb}), .in_1({12{1'b0}}), .out(multiplexer_1_out));
  and and_1 (and_1_out, ~dIn[0], ~dIn[1], ~dIn[2], ~dIn[3], F);  // And
  and and_2 (and_2_out, ~IR3, ~IR2, ~logSelect[0], ~logSelect[1]);  // And
  Multiplexer multiplexer_2 (.sel(logSelect[1]), .in_0(NE), .in_1(GE), .out(multiplexer_2_out));
  xor xor_1 (xor_1_out, multiplexer_2_out, ~alt);  // XOr
  D_FF d_ff_1 (.D(reset), .C(clock), .Q(rst));  // open: nQ
  Register #(.Bits(16)) IR (.D(dIn), .C(clock), .en(F), .Q({IR_q, Rb, IR3, IR2, logSelect[0], logSelect[1]}));
  Register #(.Bits(12)) IM (.D(multiplexer_1_out), .C(clock), .en(F), .Q(IM_q[15:4]));
  D_FF fetch (.D(or_1_out), .C(clock), .Q(F), .nQ(E));
  // Probe IR on {IR_q, Rb, IR3, IR2, logSelect[0], logSelect[1]}
  or or_1 (or_1_out, E, rst, and_1_out);
  Register prefix (.D(and_2_out), .C(clock), .en(F), .Q(prefix_q));
  D_FF d_ff_2 (.D(E), .C(clock), .Q(d_ff_2_q));  // open: nQ
  or or_2 (imm_t, prefix_q, ~IR3);  // Or
  or or_3 (or_3_out, logSelect[0], logSelect[1]);
  // Probe fetch on F
  D_FF d_ff_3 (.D(xor_1_out), .C(clock), .Q(cond));  // open: nQ
  // Probe cond on cond
  and and_3 (JorB, ~IR3, ~IR2, or_3_out);  // And
  and and_4 (and_4_out, ~multiplexer_4_out[4], zS1);  // And
  and and_5 (and_5_out, logSelect[0], ~cond);  // And
  and and_6 (and_6_out, JorB, ~F);  // And
  r0 r0_1 (.rin(IR_q[11:8]), .pc(multiplexer_4_out[4]), .rout(Ra), .z(zS1));
  execPLA execpla_1 (
    .IR3(IR3), .IR2(IR2), .IR1(logSelect[0]), .IR0(logSelect[1]), .imm(imm_t), .selImm(execpla_1_selimm[0]),
    .selConst(execpla_1_selimm[1]), .sub(execpla_1_selimm[2]), .\logic (execpla_1_selimm[3]),
    .aPC(execpla_1_selimm[4]), .lowImm(execpla_1_selimm[5]), .rd(execpla_1_selimm[6]),
    .wr(execpla_1_selimm[7]), .we(execpla_1_we), .sign(execpla_1_selimm[9]), .word(execpla_1_selimm[10]),
    .selRd(execpla_1_selimm[11]), .slt(execpla_1_selimm[12]));
  or or_4 (or_4_out[4], logSelect[0], ~JorB, ~alt);  // Or
  and and_7 (or_4_out[5], logSelect[0], JorB);
  nor nor_1 (nor_1_out[1], and_10_out, rst);
  or or_5 (Azero, rst, and_4_out);
  r0 r0_2 (.rin(IR_q[15:12]), .pc(F), .rout(Rw), .z(zD));
  and and_8 (zS2, ~Rb[0], ~Rb[1], ~Rb[2], ~Rb[3]);  // And
  or or_6 (or_4_out[1], and_5_out, ~JorB, rst);  // Or
  and and_9 (execpla_1_selimm[8], ~zD, execpla_1_we);  // And
  or or_7 (or_7_out, and_6_out, ~rst);  // Or
  Multiplexer #(.Bits(4)) multiplexer_3 (
    .sel(multiplexer_4_out[5]), .in_0(Rb), .in_1(IR_q[15:12]), .out({multiplexer_3_out, alt}));
  and and_10 (and_10_out, ~F, zS2, ~multiplexer_4_out[0]);  // And
  Multiplexer #(.Bits(13)) multiplexer_4 (
    .sel(F), .in_0(execpla_1_selimm), .in_1({7'b0000101, or_4_out[5:4], 2'b00, or_4_out[1], 1'b1}),
    .out({slt, selRd, word, sign, we, wr, rd, multiplexer_4_out[5:4], \logic , sub, multiplexer_4_out[1:0]}));
  and and_11 (IM_q[0], ~or_7_out, alt);  // And
  or or_8 (selImm, and_10_out, multiplexer_4_out[0]);
  or or_9 (or_9_out, and_10_out, multiplexer_4_out[1]);
  Multiplexer #(.Bits(16)) multiplexer_5 (
    .sel(or_9_out), .in_0({IM_q[15:4], multiplexer_3_out, IM_q[0]}), .in_1({{14{1'b0}}, nor_1_out[1], 1'b0}),
    .out(Imm));
  // Probe IM on Imm

  // Other names for the same wires on the sheet: IR0 = logSelect[1]; IR1 = logSelect[0]

  // Notes on the sheet:
  //   clock: controls internal registers
  //   reset: when high forces the PC to 0x0000
  //   dIn: data from memory
  //   NE: A ~= B
  //   GE: A >= B
  //   wr: memory write cycle
  //   rd: memory read cycle
  //   sign: not LBU
  //   word: not SB, LB or LBU
  //   sub: change addition to subtraction
  //   logic: select logic operation instead of addition
  //   logSelect: selects between shift right, AND, OR, XOR
  //   Imm: saved from prefix instruction and 4 bits from the current instruction
  //   selImm: B is immediate
  //   Azero: force A to 0
  //   we: updates register Rw
  //   Rw: register to be written
  //   Ra: first register to read
  //   Rb: second register to read
  //   selRd: selects betweenALU result and memory for write back
  //   slt: ignores ALU result and use GE?0x0000:0x0001
endmodule
