// Digital circuit drv16.dig as structural Verilog
// 16 bit processor which is compatible at the assembly language level with RISC-V
module drv16 (
  input  clock,
  input  reset,
  input  [15:0] dIn,
  output [14:0] addr,
  output wr,
  output [15:0] dOut,
  output rd
);

  wire adapt_1_alt, ALU_ge, ALU_ne, controlunit_1_azero, controlunit_1_const2, controlunit_1_even,
       controlunit_1_immlow, controlunit_1_logic, controlunit_1_selconst, controlunit_1_selimm,
       controlunit_1_selrd, controlunit_1_sign, controlunit_1_slt, controlunit_1_sub, controlunit_1_we,
       controlunit_1_word;
  wire [0:0] ALU_r, not_1_out;
  wire [1:0] controlunit_1_logselect;
  wire [3:0] controlunit_1_ra, controlunit_1_rb, controlunit_1_rw;
  wire [11:0] controlunit_1_topimm;
  wire [15:0] adapt_1_a, adapt_1_b, bytes_1_tord, multiplexer_1_out, multiplexer_2_out, registerfile_1_da,
       registerfile_1_db;

  controlUnit controlunit_1 (
    .clock(clock), .reset(reset), .dIn(dIn), .alt(adapt_1_alt), .NE(ALU_ne), .GE(ALU_ge), .wr(wr), .rd(rd),
    .sign(controlunit_1_sign), .word(controlunit_1_word), .sub(controlunit_1_sub),
    .\logic (controlunit_1_logic), .logSelect(controlunit_1_logselect), .topImm(controlunit_1_topimm),
    .even(controlunit_1_even), .const2(controlunit_1_const2), .selImm(controlunit_1_selimm),
    .selConst(controlunit_1_selconst), .Azero(controlunit_1_azero), .we(controlunit_1_we),
    .Rw(controlunit_1_rw), .Ra(controlunit_1_ra), .Rb(controlunit_1_rb), .selRd(controlunit_1_selrd),
    .slt(controlunit_1_slt), .immLow(controlunit_1_immlow));
  // Probe selCont on controlunit_1_selconst
  not not_1 (not_1_out[0], ALU_ge);
  Multiplexer #(.Bits(16)) multiplexer_1 (
    .sel(controlunit_1_slt), .in_0({addr, ALU_r[0]}), .in_1({{15{1'b0}}, not_1_out[0]}),
    .out(multiplexer_1_out));
  // Probe rS2 on controlunit_1_rb
  // Probe rS1 on controlunit_1_ra
  // Probe rD on controlunit_1_rw
  Multiplexer #(.Bits(16)) multiplexer_2 (
    .sel(controlunit_1_selrd), .in_0(multiplexer_1_out), .in_1(bytes_1_tord), .out(multiplexer_2_out));
  // Probe selImm on controlunit_1_selimm
  // Probe we on controlunit_1_we
  RegisterFile #(.AddrBits(4), .Bits(16)) registerfile_1 (
    .Din(multiplexer_2_out), .we(controlunit_1_we), .Rw(controlunit_1_rw), .C(clock), .Ra(controlunit_1_ra),
    .Rb(controlunit_1_rb), .Da(registerfile_1_da), .Db(registerfile_1_db));
  // Probe dA on registerfile_1_da
  // Probe dB on registerfile_1_db
  adapt adapt_1 (
    .Da(registerfile_1_da), .Db(registerfile_1_db), .topImm(controlunit_1_topimm), .rD(controlunit_1_rw),
    .rS2(controlunit_1_rb), .even(controlunit_1_even), .const2(controlunit_1_const2),
    .selImm(controlunit_1_selimm), .selConst(controlunit_1_selconst), .Azero(controlunit_1_azero),
    .immLow(controlunit_1_immlow), .A(adapt_1_a), .B(adapt_1_b), .alt(adapt_1_alt));
  bytes bytes_1 (
    .dIn(dIn), .sign(controlunit_1_sign), .word(controlunit_1_word), .A0(ALU_r[0]),
    .fromRS2(registerfile_1_db), .dOut(dOut), .toRD(bytes_1_tord));
  // Probe A on adapt_1_a
  alu ALU (
    .R({addr, ALU_r[0]}), .A(adapt_1_a), .B(adapt_1_b), .sub(controlunit_1_sub),
    .logSelect(controlunit_1_logselect), .\logic (controlunit_1_logic), .NE(ALU_ne), .GE(ALU_ge));
  // Probe B on adapt_1_b
  // Probe NE on ALU_ne
  // Probe GE on ALU_ge

  // Notes on the sheet:
  //   addr: selects a 16 bit word in memory to be read or changed
  //   wr: indicates a write operation
  //   dOut: word to be sent to memory
  //   reset: when high prepares the processor to execute from address 0
  //   dIn: word coming from memory
  //   rd: indicates that memory will be read in this cycle
endmodule
