// Digital circuit system.dig as structural Verilog
// A simple system with a drv16 processor, 64KB of RAM, a terminal and keyboard
module system (
  input  clk
);

  wire and_1_out, and_2_out, comparator_1_eq, cpu_p6, cpu_p7, cpu_p8, reset_out;
  wire [7:0] mem0_low_d, mem1_high_d;
  wire [14:0] cpu_p4;
  wire [15:0] cpu_p5, keyboard_1_d, multiplexer_1_out;

  Keyboard keyboard_1 (.C(clk), .en(and_1_out), .D(keyboard_1_d));  // open: av
  DipSwitch reset (.out(reset_out));
  // Probe dIn on multiplexer_1_out
  Multiplexer #(.Bits(16)) multiplexer_1 (
    .sel(comparator_1_eq), .in_0({mem1_high_d, mem0_low_d}), .in_1(keyboard_1_d), .out(multiplexer_1_out));
  // drv16 cpu: pin names not known; wires that end beside it: clk, reset_out, multiplexer_1_out, cpu_p4, cpu_p5, cpu_p6, cpu_p7, cpu_p8
  and and_1 (and_1_out, cpu_p6, comparator_1_eq);
  // Probe addr on cpu_p4
  Comparator #(.Bits(15)) comparator_1 (.a({15{1'b1}}), .b(cpu_p4), .eq(comparator_1_eq));  // open: gt, lt
  RAMDualPort #(.AddrBits(15), .isProgramMemory("true"), .Bits(8)) mem0_low (
    .A(cpu_p4), .Din(cpu_p5[7:0]), .str(cpu_p8), .C(clk), .ld(cpu_p6), .D(mem0_low_d));
  RAMDualPort #(.AddrBits(15), .isProgramMemory("true"), .Bits(8)) mem1_high (
    .A(cpu_p4), .Din(cpu_p5[15:8]), .str(cpu_p7), .C(clk), .ld(cpu_p6), .D(mem1_high_d));
  and and_2 (and_2_out, comparator_1_eq, cpu_p8);
  Terminal terminal_1 (.D(cpu_p5), .C(clk), .en(and_2_out));

  // Notes on the sheet:
  //   clk: Hz: 2147483647
endmodule
